# Fritzing sketch rasp-arduino-i2c (saved by Fritzing 0.9.2b)
circuit board: 8.46667cm x 5.64444cm
breadboards: 1

parts:
  Potentiomètre = Arduino Uno (Rev3)
  Raspberry_Pi_2 = Raspberry Pi 2
  R1 = Resistor [tolerance=±5% resistance=220 package="1206 [SMD]"]
  Buzzer = Piezo Speaker
  R2 = TRIMPOT [package=3386u]

nets:
  N1: Potentiomètre.A0, R2.WIPER
  N2: Potentiomètre.A4/SDA, Raspberry_Pi_2.GPIO2
  N3: Potentiomètre.D9_PWM, R1.Pin_0
  GND: Potentiomètre.GND, Raspberry_Pi_2.GND, Buzzer.pin2, R2.CCW
  N4: Potentiomètre.A5/SCL, Raspberry_Pi_2.GPIO3
  N5: Potentiomètre.5V, R2.CW
  N6: R1.Pin_1, Buzzer.pin1
